# Fritzing sketch interphone 3 2 (saved by Fritzing 1.0.8)
breadboards: 1

parts:
  M1 = DOIT Esp32 DevKit v1 (30 pins long, 11 pins width) [part_number=ESP32S-PIN30]
  R1 = Resistor [tolerance=±5% power=0.25W resistance=330 package=THT]
  R2 = Resistor [tolerance=±5% power=0.25W resistance=330 package=THT]
  R3 = Resistor [tolerance=±5% power=0.25W resistance=1k package=THT]
  LED1 = LED - 5mm [color="Red (633nm)" current=0.030A package="5 mm [THT]"]
  LED2 = LED - 5mm [color="Red (633nm)" current=0.030A package="5 mm [THT]"]
  D1 = Rectifier Diode [part_number=1N4001 package="300 mil [THT]"]
  R4 = Resistor [tolerance=±5% power=0.25W resistance=10k package=THT]
  Q1 = TRANSISTOR_NPN [package=to-92]
  J1 = Buzzer
  S1 = Pushbutton [package="[THT]"]
  Part1 = KY-019 5V Relay Module [package="Breakout board"]

nets:
  N1: M1.3V3, R4.Pin_0
  N2: M1.GND, LED1.cathode, LED2.cathode, Q1.E, S1.Pin_1, S1.Pin_2, Part1.-
  N3: M1.D18, R3.Pin_0
  N4: M1.D19, R2.Pin_0
  N5: M1.D21, R4.Pin_1, S1.Pin_3, S1.Pin_4
  N6: M1.D13, Part1.S
  N7: M1.VIN, D1.cathode, J1.pin2, Part1.+, Part1.Common
  N8: R1.Pin_0, Part1.NO
  N9: R1.Pin_1, LED1.anode
  N10: R2.Pin_1, LED2.anode
  N11: R3.Pin_1, Q1.B
  N12: D1.anode, Q1.C, J1.pin1

custom parts:
  DOIT Esp32 DevKit v1 (30 pins long, 11 pins width): The DOIT Esp32 DevKit v1 is one of the development board created by DOIT to evaluate the ESP-WROOM-32 module. It is based on the ESP32 microcontroller that boasts Wifi, Bluetooth, Ethernet and Low Power support all in a single chip. (vanepp) made breadboard work, adjusted pin numbering and labels and reduced size of schematic and cleaned up pcb. This chip is 30pins long (2 x15) and 11 pins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
  Buzzer: Fixed frequency buzzer
  KY-019 5V Relay Module: KY-019 5V Relay module, used to control AC circuits.
